// Logisim project riscv.circ as structural Verilog
module main (
  input  in_1
);

  wire and_1_out, avxalu_1_zero, Clk_out, controlmodule_1_alusrc, controlmodule_1_branch,
       controlmodule_1_memwrite, controlmodule_1_regwrite, Reset_out;
  wire [1:0] controlmodule_1_aluop, controlmodule_1_memtoreg;
  wire [3:0] alucontrol_1_operation;
  wire [15:0] bitselector_1_out, bitselector_2_out;
  wire [31:0] adder_1_out, adder_2_out, avxalu_1_s, DataMemory_dout, IntructionMemory_dout,
       multiplexer_1_out, multiplexer_2_out, multiplexer_3_out, PC_q, registerfile_1_readdata1,
       registerfile_1_readdata2, undriven;

  // Probe on multiplexer_2_out
  Button Clk (.out(Clk_out));
  Button Reset (.out(Reset_out));
  Register #(.width(32)) PC (.D(multiplexer_2_out), .en(1'b1), .clk(Clk_out), .Q(PC_q), .clr(Reset_out));
  BitSelector #(.group(16), .width(32)) bitselector_1 (.in(PC_q), .out(bitselector_1_out), .sel(1'b0));
  RAM #(.addrWidth(16), .dataWidth(32), .enables("line")) IntructionMemory (
    .addr(bitselector_1_out), .clk(Clk_out), .dout(IntructionMemory_dout));  // open: we, din
  Adder #(.width(32)) adder_1 (.a(32'h1), .b(PC_q), .out(adder_1_out));  // open: cin, cout
  // Probe on IntructionMemory_dout[6:0]
  // Probe on IntructionMemory_dout[31:25]
  // Probe on IntructionMemory_dout[11:7]
  // Probe on IntructionMemory_dout[19:15]
  // Probe on IntructionMemory_dout[24:20]
  // Probe on IntructionMemory_dout[14:12]
  controlModule controlmodule_1 (
    .opcode(IntructionMemory_dout[6:0]), .Branch(controlmodule_1_branch),
    .MemtoReg(controlmodule_1_memtoreg[0]), .ALUOp(controlmodule_1_aluop),
    .MemWrite(controlmodule_1_memwrite), .ALUSrc(controlmodule_1_alusrc), .RegWrite(controlmodule_1_regwrite));  // open: MemRead
  registerFile registerfile_1 (
    .readReg1(IntructionMemory_dout[19:15]), .readReg2(IntructionMemory_dout[24:20]),
    .writeData(multiplexer_3_out), .writeEnable(controlmodule_1_regwrite), .reset(Reset_out), .clk(Clk_out),
    .readData1(registerfile_1_readdata1), .readData2(registerfile_1_readdata2));  // open: writeRegister
  Multiplexer #(.width(32)) multiplexer_1 (
    .in0(registerfile_1_readdata2), .in1(undriven), .out(multiplexer_1_out), .sel(controlmodule_1_alusrc));
  Adder #(.width(32)) adder_2 (.a(PC_q), .b(undriven), .out(adder_2_out));  // open: cin, cout
  ALUControl alucontrol_1 (
    .ALUOp(controlmodule_1_aluop), .func7(IntructionMemory_dout[31:25]),
    .func3(IntructionMemory_dout[14:12]), .operation(alucontrol_1_operation));
  avxALU avxalu_1 (
    .A(registerfile_1_readdata1), .B(multiplexer_1_out), .mode(in_1), .S(avxalu_1_s), .zero(avxalu_1_zero));  // open: vecSize
  and and_1 (and_1_out, controlmodule_1_branch, avxalu_1_zero);
  RAM #(.addrWidth(16), .dataWidth(32), .enables("line")) DataMemory (
    .addr(bitselector_2_out), .we(controlmodule_1_memwrite), .clk(Clk_out), .din(registerfile_1_readdata2),
    .dout(DataMemory_dout));
  BitSelector #(.group(16), .width(32)) bitselector_2 (.in(avxalu_1_s), .out(bitselector_2_out), .sel(1'b0));
  Multiplexer #(.width(32)) multiplexer_2 (
    .in0(adder_1_out), .in1(adder_2_out), .out(multiplexer_2_out), .sel(and_1_out));
  Multiplexer #(.select(2), .width(32)) multiplexer_3 (
    .in0(adder_1_out), .in1(adder_2_out), .in2(DataMemory_dout), .in3(avxalu_1_s), .out(multiplexer_3_out),
    .sel(controlmodule_1_memtoreg));
  // Pins of 1 and 2 bits meet at controlmodule_1_memtoreg
endmodule

module registerFile (
  input  [4:0] readReg1,
  input  [4:0] readReg2,
  input  [4:0] writeRegister,
  input  [31:0] writeData,
  input  writeEnable,
  input  reset,
  input  clk,
  output [31:0] readData1,
  output [31:0] readData2
);

  wire and_1_out, decoder_1_out0, decoder_1_out1, decoder_1_out2, decoder_1_out3, decoder_1_out4,
       decoder_1_out5, decoder_1_out6, decoder_1_out7, decoder_1_out8, decoder_1_out9, decoder_1_out10,
       decoder_1_out11, decoder_1_out12, decoder_1_out13, decoder_1_out14, decoder_1_out15, decoder_1_out16,
       decoder_1_out17, decoder_1_out18, decoder_1_out19, decoder_1_out20, decoder_1_out21, decoder_1_out22,
       decoder_1_out23, decoder_1_out24, decoder_1_out25, decoder_1_out26, decoder_1_out27, decoder_1_out28,
       decoder_1_out29, decoder_1_out30, decoder_1_out31, not_1_out;
  wire [31:0] register_1_q, register_2_q, register_3_q, register_4_q, register_5_q, register_6_q,
       register_7_q, register_8_q, register_9_q, register_10_q, register_11_q, register_12_q, register_13_q,
       register_14_q, register_15_q, register_16_q, register_17_q, register_18_q, register_19_q,
       register_20_q, register_21_q, register_22_q, register_23_q, register_24_q, register_25_q,
       register_26_q, register_27_q, register_28_q, register_29_q, register_30_q, register_31_q,
       register_32_q;

  Decoder #(.select(5)) decoder_1 (
    .out0(decoder_1_out0), .out1(decoder_1_out1), .out2(decoder_1_out2), .out3(decoder_1_out3),
    .out4(decoder_1_out4), .out5(decoder_1_out5), .out6(decoder_1_out6), .out7(decoder_1_out7),
    .out8(decoder_1_out8), .out9(decoder_1_out9), .out10(decoder_1_out10), .out11(decoder_1_out11),
    .out12(decoder_1_out12), .out13(decoder_1_out13), .out14(decoder_1_out14), .out15(decoder_1_out15),
    .out16(decoder_1_out16), .out17(decoder_1_out17), .out18(decoder_1_out18), .out19(decoder_1_out19),
    .out20(decoder_1_out20), .out21(decoder_1_out21), .out22(decoder_1_out22), .out23(decoder_1_out23),
    .out24(decoder_1_out24), .out25(decoder_1_out25), .out26(decoder_1_out26), .out27(decoder_1_out27),
    .out28(decoder_1_out28), .out29(decoder_1_out29), .out30(decoder_1_out30), .out31(decoder_1_out31),
    .sel(writeRegister), .en(and_1_out));
  not not_1 (not_1_out, clk);
  and and_1 (and_1_out, writeEnable, not_1_out);
  Register #(.width(32)) register_1 (.D({32{1'b0}}), .en(decoder_1_out0), .clk(clk), .Q(register_1_q), .clr(reset));
  Register #(.width(32)) register_2 (.D(writeData), .en(decoder_1_out1), .clk(clk), .Q(register_2_q), .clr(reset));
  Register #(.width(32)) register_3 (.D(writeData), .en(decoder_1_out2), .clk(clk), .Q(register_3_q), .clr(reset));
  Register #(.width(32)) register_4 (.D(writeData), .en(decoder_1_out3), .clk(clk), .Q(register_4_q), .clr(reset));
  Register #(.width(32)) register_5 (.D(writeData), .en(decoder_1_out4), .clk(clk), .Q(register_5_q), .clr(reset));
  Register #(.width(32)) register_6 (.D(writeData), .en(decoder_1_out5), .clk(clk), .Q(register_6_q), .clr(reset));
  Register #(.width(32)) register_7 (.D(writeData), .en(decoder_1_out6), .clk(clk), .Q(register_7_q), .clr(reset));
  Register #(.width(32)) register_8 (.D(writeData), .en(decoder_1_out7), .clk(clk), .Q(register_8_q), .clr(reset));
  Register #(.width(32)) register_9 (.D(writeData), .en(decoder_1_out8), .clk(clk), .Q(register_9_q), .clr(reset));
  Register #(.width(32)) register_10 (.D(writeData), .en(decoder_1_out9), .clk(clk), .Q(register_10_q), .clr(reset));
  Register #(.width(32)) register_11 (.D(writeData), .en(decoder_1_out10), .clk(clk), .Q(register_11_q), .clr(reset));
  Register #(.width(32)) register_12 (.D(writeData), .en(decoder_1_out11), .clk(clk), .Q(register_12_q), .clr(reset));
  Register #(.width(32)) register_13 (.D(writeData), .en(decoder_1_out12), .clk(clk), .Q(register_13_q), .clr(reset));
  Register #(.width(32)) register_14 (.D(writeData), .en(decoder_1_out13), .clk(clk), .Q(register_14_q), .clr(reset));
  Register #(.width(32)) register_15 (.D(writeData), .en(decoder_1_out14), .clk(clk), .Q(register_15_q), .clr(reset));
  Register #(.width(32)) register_16 (.D(writeData), .en(decoder_1_out15), .clk(clk), .Q(register_16_q), .clr(reset));
  Register #(.width(32)) register_17 (.D(writeData), .en(decoder_1_out16), .clk(clk), .Q(register_17_q), .clr(reset));
  Register #(.width(32)) register_18 (.D(writeData), .en(decoder_1_out17), .clk(clk), .Q(register_18_q), .clr(reset));
  Register #(.width(32)) register_19 (.D(writeData), .en(decoder_1_out18), .clk(clk), .Q(register_19_q), .clr(reset));
  Register #(.width(32)) register_20 (.D(writeData), .en(decoder_1_out19), .clk(clk), .Q(register_20_q), .clr(reset));
  Register #(.width(32)) register_21 (.D(writeData), .en(decoder_1_out20), .clk(clk), .Q(register_21_q), .clr(reset));
  Register #(.width(32)) register_22 (.D(writeData), .en(decoder_1_out21), .clk(clk), .Q(register_22_q), .clr(reset));
  Register #(.width(32)) register_23 (.D(writeData), .en(decoder_1_out22), .clk(clk), .Q(register_23_q), .clr(reset));
  Register #(.width(32)) register_24 (.D(writeData), .en(decoder_1_out23), .clk(clk), .Q(register_24_q), .clr(reset));
  Register #(.width(32)) register_25 (.D(writeData), .en(decoder_1_out24), .clk(clk), .Q(register_25_q), .clr(reset));
  Register #(.width(32)) register_26 (.D(writeData), .en(decoder_1_out25), .clk(clk), .Q(register_26_q), .clr(reset));
  Register #(.width(32)) register_27 (.D(writeData), .en(decoder_1_out26), .clk(clk), .Q(register_27_q), .clr(reset));
  Register #(.width(32)) register_28 (.D(writeData), .en(decoder_1_out27), .clk(clk), .Q(register_28_q), .clr(reset));
  Register #(.width(32)) register_29 (.D(writeData), .en(decoder_1_out28), .clk(clk), .Q(register_29_q), .clr(reset));
  Register #(.width(32)) register_30 (.D(writeData), .en(decoder_1_out29), .clk(clk), .Q(register_30_q), .clr(reset));
  Register #(.width(32)) register_31 (.D(writeData), .en(decoder_1_out30), .clk(clk), .Q(register_31_q), .clr(reset));
  Register #(.width(32)) register_32 (.D(writeData), .en(decoder_1_out31), .clk(clk), .Q(register_32_q), .clr(reset));
  Multiplexer #(.select(5), .width(32)) multiplexer_1 (
    .in0(register_1_q), .in1(register_2_q), .in2(register_3_q), .in3(register_4_q), .in4(register_5_q),
    .in5(register_6_q), .in6(register_7_q), .in7(register_8_q), .in8(register_9_q), .in9(register_10_q),
    .in10(register_11_q), .in11(register_12_q), .in12(register_13_q), .in13(register_14_q),
    .in14(register_15_q), .in15(register_16_q), .in16(register_17_q), .in17(register_18_q),
    .in18(register_19_q), .in19(register_20_q), .in20(register_21_q), .in21(register_22_q),
    .in22(register_23_q), .in23(register_24_q), .in24(register_25_q), .in25(register_26_q),
    .in26(register_27_q), .in27(register_28_q), .in28(register_29_q), .in29(register_30_q),
    .in30(register_31_q), .in31(register_32_q), .out(readData2), .sel(readReg2));
  Multiplexer #(.select(5), .width(32)) multiplexer_2 (
    .in0(register_1_q), .in1(register_2_q), .in2(register_3_q), .in3(register_4_q), .in4(register_5_q),
    .in5(register_6_q), .in6(register_7_q), .in7(register_8_q), .in8(register_9_q), .in9(register_10_q),
    .in10(register_11_q), .in11(register_12_q), .in12(register_13_q), .in13(register_14_q),
    .in14(register_15_q), .in15(register_16_q), .in16(register_17_q), .in17(register_18_q),
    .in18(register_19_q), .in19(register_20_q), .in20(register_21_q), .in21(register_22_q),
    .in22(register_23_q), .in23(register_24_q), .in24(register_25_q), .in25(register_26_q),
    .in26(register_27_q), .in27(register_28_q), .in28(register_29_q), .in29(register_30_q),
    .in30(register_31_q), .in31(register_32_q), .out(readData1), .sel(readReg1));
endmodule

module avxALUTstVector (
  input  [31:0] A,
  input  [31:0] B,
  input  [1:0] vecSize,
  input  mode,
  output [31:0] S,
  output zero
);

  avxALU avxalu_1 (.A(A), .B(B), .vecSize(vecSize), .mode(mode), .S(S), .zero(zero));
endmodule

// VHDL entity avxALU, as the project stores it:
library ieee;
use ieee.std_logic_1164.all;
use ieee.numeric_std.all;
 
entity avxALU is
  port (
	A  : in std_logic_vector(31 downto 0);
	B  : in std_logic_vector(31 downto 0);
	 
	vecSize : in std_logic_vector(1 downto 0);
	mode : in std_logic;
	 
	S   : out std_logic_vector(31 downto 0);

	zero : out std_logic
    );
end avxALU;
 
 
architecture rtl of avxALU is
 
  signal w_G : std_logic_vector(31 downto 0); -- Generate
  signal w_P : std_logic_vector(31 downto 0); -- Propagate
  signal w_C : std_logic_vector(32 downto 0);   -- Carry
 
  signal w_SUM  : std_logic_vector(31 downto 0);

  signal BB : std_logic_vector(31 downto 0);
  
begin

 	gen_B : for ii in 0 to 31 generate
		b_inst : BB(ii) <= B(ii) when mode = '0' else B(ii) xor '1';
	end generate gen_B;
  	w_C(0) <= mode;
	
  -- Create the Full Adders
	GEN_FULL_ADDERS : for ii in 0 to 31 generate
		FULL_ADDER_INST : w_SUM(ii) <= A(ii) xor BB(ii) xor w_C(ii);
	end generate GEN_FULL_ADDERS;
 
  -- Create the Generate (G) Terms:  Gi=Ai*Bi
  -- Create the Propagate Terms: Pi=Ai+Bi
  -- Create the Carry Terms:
	GEN_CLA : for jj in 0 to 31 generate
		w_G(jj)   <= A(jj) and BB(jj);
		w_P(jj)   <= A(jj) or BB(jj);
		--if ((vecSize = "00") and boolean(jj mod 4)) then
		w_C(jj+1) <= mode when ( ( (((jj+1) mod 4) = 0) and (vecSize = "00")) or ( (((jj+1) mod 8) = 0) and (vecSize = "01")) or ( (((jj+1) mod 16) = 0) and (vecSize = "10")))
					else w_G(jj) or (w_P(jj) and w_C(jj));
	end generate GEN_CLA;
	
     
 
  S <= w_SUM;  -- VHDL Concatenation

  zero <= '1' when w_SUM = x"00000000" else '0';
  	
end rtl;

// VHDL entity controlModule, as the project stores it:
--------------------------------------------------------------------------------
-- Project :
-- File    :
-- Autor   :
-- Date    :
--
--------------------------------------------------------------------------------
-- Description :
--
--------------------------------------------------------------------------------

LIBRARY ieee;
USE ieee.std_logic_1164.all;

ENTITY controlModule IS
  PORT (
  ------------------------------------------------------------------------------
  --Insert input ports below
    opcode 	: in std_logic_vector(6 downto 0);

    Branch 	: out std_logic;
    MemRead 	: out std_logic;
    MemtoReg 	: out std_logic;
    ALUOp 	: out std_logic_vector(1 downto 0);
    MemWrite 	: out std_logic;
    ALUSrc	: out std_logic;
    RegWrite	: out std_logic
    );
END controlModule;


ARCHITECTURE TypeArchitecture OF controlModule IS

BEGIN

process (opcode) is begin
	case opcode is
		when "0110011" => -- R-type OK
			ALUSrc	<= '0';
			MemtoReg 	<= '0';
			RegWrite	<= '1';
			MemRead 	<= '0';
			MemWrite 	<= '0';
			Branch 	<= '0';
			ALUOp 	<= "10";
		when "0010011" => -- I-type + SLLI + SRLI ok?
			ALUSrc	<= '1';
			MemtoReg 	<= '0';
			RegWrite	<= '1';
			MemRead 	<= '0';
			MemWrite 	<= '0';
			Branch 	<= '0';
			ALUOp 	<= "10";
		when "0010111" => -- AUIPC add upperimmediate to PC ok?
			ALUSrc	<= '1';
			MemtoReg 	<= '0';
			RegWrite	<= '1';
			MemRead 	<= '0';
			MemWrite 	<= '0';
			Branch 	<= '0';
			ALUOp 	<= "10";
		when "0000011" => --lw OK
			ALUSrc	<= '1';
			MemtoReg 	<= '1';
			RegWrite	<= '1';
			MemRead 	<= '1';
			MemWrite 	<= '0';
			Branch 	<= '0';
			ALUOp 	<= "00";
		when "0110111" => --lui ok?
			ALUSrc	<= '1';
			MemtoReg 	<= '0';
			RegWrite	<= '1';
			MemRead 	<= '0';
			MemWrite 	<= '0';
			Branch 	<= '0';
			ALUOp 	<= "00";
		when "0100011" => --sw OK
			ALUSrc	<= '1';
			MemtoReg 	<= '-';
			RegWrite	<= '0';
			MemRead 	<= '0';
			MemWrite 	<= '1';
			Branch 	<= '0';
			ALUOp 	<= "00";
		when "1101111" => --jal 
			ALUSrc	<= '1';
			MemtoReg 	<= '-';
			RegWrite	<= '0';
			MemRead 	<= '0';
			MemWrite 	<= '1';
			Branch 	<= '1';
			ALUOp 	<= "00";
		when "1100111" => --jalr 
			ALUSrc	<= '1';
			MemtoReg 	<= '-';
			RegWrite	<= '0';
			MemRead 	<= '0';
			MemWrite 	<= '1';
			Branch 	<= '0';
			ALUOp 	<= "00";
		when "1100011" => --beq + bneq OK
			ALUSrc	<= '0';
			MemtoReg 	<= '-';
			RegWrite	<= '0';
			MemRead 	<= '0';
			MemWrite 	<= '0';
			Branch 	<= '1';
			ALUOp 	<= "01";
		when others =>
			ALUSrc	<= '0';
			MemtoReg 	<= '0';
			RegWrite	<= '0';
			MemRead 	<= '0';
			MemWrite 	<= '0';
			Branch 	<= '0';
			ALUOp 	<= "00";
	end case;
end process;

END TypeArchitecture;

// VHDL entity ALUControl, as the project stores it:
LIBRARY ieee;
USE ieee.std_logic_1164.all;

ENTITY ALUControl IS
  PORT (
  ------------------------------------------------------------------------------
  --Insert input ports below
    ALUOp 	: in std_logic_vector(1 downto 0);
    func7 	: in std_logic_vector(6 downto 0);
    func3 	: in std_logic_vector(2 downto 0);

    operation 	: out std_logic_vector(3 downto 0)
    );
END ALUControl;


ARCHITECTURE TypeArchitecture OF ALUControl IS

BEGIN

process (ALUOp, func7, func3) is begin
	case ALUOp is
		when "00" => 
			operation <= "0010"; --add
		when "-1" => 
			operation <= "0110"; --sub
		when "1-" => 
			case func7 & func3 is
				when "0000000000" =>
					operation <= "0010"; --add
				when "0100000000" =>
					operation <= "0110"; --sub
				when "0000000111" =>
					operation <= "0000"; --and
				when "0000000110" =>
					operation <= "0001"; --or
				when others =>
					operation <= "0000";
			end case;
		when others =>
			operation <= "0000";
	end case;
end process;

END TypeArchitecture;

// VHDL entity immediateGenerator, as the project stores it:
--------------------------------------------------------------------------------
-- Project :
-- File    :
-- Autor   :
-- Date    :
--
--------------------------------------------------------------------------------
-- Description :
--
--------------------------------------------------------------------------------

LIBRARY ieee;
USE ieee.std_logic_1164.all;

ENTITY immediateGenerator IS
  PORT (
	instruction	: in std_logic_vector(31 downto 0);
	immediate 	: out std_logic vector(31 downto 0);
	
    );
END immediateGenerator;

--------------------------------------------------------------------------------
--Complete your VHDL description below
--------------------------------------------------------------------------------

ARCHITECTURE TypeArchitecture OF immediateGenerator IS

BEGIN

	

END TypeArchitecture;
